# Fritzing sketch circuiti (saved by Fritzing 0.9.9b)

parts:
  WeMos_D1_Mini1 = WeMos D1 Mini
  A1 = AS5600 module
  R1 = Rotary Potentiometer (Small) [maximum_resistance=100kΩ package=THT]

nets:
  N1: WeMos_D1_Mini1.3V3, A1.Pin_1, R1.leg1
  N2: WeMos_D1_Mini1.A0, R1.wiper
  N3: WeMos_D1_Mini1.D1, A1.Pin_6
  N4: WeMos_D1_Mini1.D2, A1.Pin_5
  N5: WeMos_D1_Mini1.D5, A1.Pin_7
  N6: WeMos_D1_Mini1.G, A1.Pin_3, R1.leg2

custom parts:
  WeMos D1 Mini: The D1 mini is a mini wifi board based on ESP-8266EX.
  AS5600 module: .This module is mainly placed behind the stepper motor to obtain the rotation angle of the stepper motor.
